// Logisim project CPU.circ as structural Verilog: 7 circuits, main circuit main
module main (
  input  RESET
);

  wire clock_1_out, cpu_1_clock_ou, cpu_1_read, cpu_1_wrt, rwcontrol_1_clkou, rwcontrol_1_wrt, xor_1_out;
  wire [15:0] cpu_1_addr, cpu_1_instruction_pointer, cpu_1_op, MEMORY_dout, rwcontrol_1_addr,
       rwcontrol_1_valou;

  Clock clock_1 (.out(clock_1_out));
  xor xor_1 (xor_1_out, clock_1_out, RESET);
  CPU cpu_1 (
    .INSTRUCTION(MEMORY_dout), .Clock_IN(xor_1_out), .Reset(RESET),
    .Instruction_Pointer(cpu_1_instruction_pointer), .ADDR(cpu_1_addr), .WRT(cpu_1_wrt), .READ(cpu_1_read),
    .Clock_OU(cpu_1_clock_ou), .OP(cpu_1_op));
  RWControl rwcontrol_1 (
    .Instr(cpu_1_instruction_pointer), .Data(cpu_1_addr), .Write(cpu_1_wrt), .Read(cpu_1_read),
    .ClkIN(cpu_1_clock_ou), .ValIN(cpu_1_op), .Addr(rwcontrol_1_addr), .WRT(rwcontrol_1_wrt),
    .ClkOU(rwcontrol_1_clkou), .ValOU(rwcontrol_1_valou));
  RAM #(.addrWidth(16), .asyncread("true"), .clearpin("true"), .dataWidth(16)) MEMORY (
    .addr(rwcontrol_1_addr), .we(rwcontrol_1_wrt), .clk(rwcontrol_1_clkou), .din(rwcontrol_1_valou),
    .dout(MEMORY_dout));  // open: oe, clr
endmodule

module CPU (
  input  [15:0] INSTRUCTION,
  input  Clock_IN,
  input  Reset,
  output [15:0] Instruction_Pointer,
  output [15:0] ADDR,
  output WRT,
  output READ,
  output Clock_OU,
  output [15:0] OP
);

  wire ADD, AMD, and_4_out, and_5_out, and_6_out, AS, BPS, BS, BUFFER2_buffer_op, BUFFER3_buffer_op,
       BUFFER6_buffer_op, buffer_1_out, buffer_2_out, buffering_1_buffer_op, buffering_2_buffer_op,
       buffering_3_buffer_op, buffering_4_buffer_op, CLOCK1, CLOCK2, CLOCK3, CLOCK4, CMP,
       controlled_buffer_1_out, CS, DS, ES, FS, IMM1_EN, IMM2_EN, IMMEDIATE_VAL_SAVE_opcode_disable, IN_DIS,
       INV_VAL, JE, JG, JL, JMP, MOV, OPCODE_DECODER_noop, or_4_out, or_5_out, OUT_ENABLE, OW, POP, PSHPOP,
       PUSH, SHL, SHR, SPS, SRC1_ENABLE, SRC2_ENABLE, SUB, WRT_t, xor_2_out, XOW;
  wire [2:0] comparator_1_gt, DST, PLA_MATRIX_out, register_2_q, SRC1, SRC2;
  wire [3:0] OPCODE;
  wire [15:0] A_q, adder_1_out, and_1_out, B_q, BP_q, C_q, D_q, E_q, F_q, IMMEDIATE_VAL_SAVE_instruction,
       multiplexer_3_out, multiplexer_4_out, multiplexer_5_out, multiplexer_6_out, multiplexer_7_out,
       multiplexer_9_out, not_1_out, or_2_out, register_1_q, shifter_1_out, shifter_2_out, SP_q, SRC1_IMM,
       SRC2_IMM, subtractor_1_out, subtractor_2_out, xor_1_out;
  wire [15:14] multiplexer_1_out;

  Buffering buffering_1 (.BUFFER_IP(Clock_IN), .BUFFER_OP(buffering_1_buffer_op));
  Register #(.width(16)) register_1 (.D(INSTRUCTION), .clk(Clock_IN), .Q(register_1_q), .clr(Reset));  // open: en
  Buffering buffering_2 (.BUFFER_IP(buffering_1_buffer_op), .BUFFER_OP(buffering_2_buffer_op));
  Multiplexer #(.width(16)) multiplexer_1 (
    .in0(register_1_q), .in1(IMMEDIATE_VAL_SAVE_instruction),
    .out({multiplexer_1_out, INV_VAL, OPCODE, SRC1, SRC2, DST}), .sel(IN_DIS));
  Buffering BUFFER1 (.BUFFER_IP(buffering_2_buffer_op), .BUFFER_OP(CLOCK1));
  IMM_SAVE IMMEDIATE_VAL_SAVE (
    .IMM_VALS(multiplexer_1_out), .INSTR_IN(register_1_q), .Clock(buffering_2_buffer_op), .Reset(Reset),
    .INSTRUCTION(IMMEDIATE_VAL_SAVE_instruction), .OPCODE_DISABLE(IMMEDIATE_VAL_SAVE_opcode_disable),
    .SRC1_IMM(IMM1_EN), .SRC1(SRC1_IMM), .SRC2_IMM(IMM2_EN), .SRC2(SRC2_IMM));
  or or_1 (IN_DIS, IMM2_EN, IMM1_EN);
  Buffering buffering_3 (.BUFFER_IP(BUFFER6_buffer_op), .BUFFER_OP(buffering_3_buffer_op));
  Buffering BUFFER5 (.BUFFER_IP(CLOCK2), .BUFFER_OP(CLOCK3));
  Buffering buffering_4 (.BUFFER_IP(buffering_3_buffer_op), .BUFFER_OP(buffering_4_buffer_op));
  Buffering BUFFER6 (.BUFFER_IP(CLOCK3), .BUFFER_OP(BUFFER6_buffer_op));
  Multiplexer multiplexer_2 (.in0(CLOCK2), .in1(buffering_4_buffer_op), .out(CLOCK4), .sel(READ));
  CPU_Decoder OPCODE_DECODER (
    .OPCODE(OPCODE), .UNENABLE(IMMEDIATE_VAL_SAVE_opcode_disable), .NOOP(OPCODE_DECODER_noop), .MOV(MOV),
    .AMD(AMD), .OW(OW), .XOW(XOW), .ADD(ADD), .SUB(SUB), .SHL(SHL), .SHR(SHR), .CMP(CMP), .JMP(JMP), .JE(JE),
    .JL(JL), .JG(JG), .WRT(WRT_t), .READ(READ), .SRC_1(SRC1_ENABLE), .SRC_2(SRC2_ENABLE), .OU(OUT_ENABLE));
  Multiplexer #(.enable("true"), .width(16)) multiplexer_3 (
    .in0(multiplexer_4_out), .in1(INSTRUCTION), .out(multiplexer_3_out), .sel(READ), .en(OUT_ENABLE));
  Multiplexer #(.width(16)) multiplexer_4 (
    .in0(multiplexer_5_out), .in1(not_1_out), .out(multiplexer_4_out), .sel(INV_VAL));
  assign not_1_out = ~multiplexer_5_out;  // NOT_Gate not_1, 16 bits wide
  Multiplexer #(.select(3), .width(16)) multiplexer_5 (
    .in0(OP), .in1(and_1_out), .in2(or_2_out), .in3(xor_1_out), .in4(shifter_1_out), .in5(shifter_2_out),
    .in6(adder_1_out), .in7(subtractor_2_out), .out(multiplexer_5_out), .sel(PLA_MATRIX_out));
  PLA #(.in_width(8), .out_width(3), .\table ("00000001 000\n00000010 001\n00000100 010\n00001000 011\n00010000 100\n00100000 101\n01000000 110\n10000000 111")) PLA_MATRIX (
    .in({SUB, ADD, SHR, SHL, XOW, OW, AMD, MOV}), .out(PLA_MATRIX_out));
  Register #(.width(16)) A (.D(multiplexer_3_out), .en(AS), .clk(CLOCK4), .Q(A_q), .clr(Reset));
  Register #(.width(16)) B (.D(multiplexer_3_out), .en(BS), .clk(CLOCK4), .Q(B_q), .clr(Reset));
  Register #(.width(16)) C (.D(multiplexer_3_out), .en(CS), .clk(CLOCK4), .Q(C_q), .clr(Reset));
  Register #(.width(16)) D (.D(multiplexer_3_out), .en(DS), .clk(CLOCK4), .Q(D_q), .clr(Reset));
  Register #(.width(16)) E (.D(multiplexer_3_out), .en(ES), .clk(CLOCK4), .Q(E_q), .clr(Reset));
  Register #(.width(16)) F (.D(multiplexer_3_out), .en(FS), .clk(CLOCK4), .Q(F_q), .clr(Reset));
  Register #(.width(16)) BP (.D(multiplexer_3_out), .en(BPS), .clk(CLOCK4), .Q(BP_q), .clr(Reset));
  Counter #(.max('hffff), .width(16)) SP (
    .clr(Reset), .load(SPS), .up(WRT_t), .count(PSHPOP), .clk(CLOCK4), .D(multiplexer_3_out), .Q(SP_q));  // open: carry
  Buffering BUFFER2 (.BUFFER_IP(CLOCK1), .BUFFER_OP(BUFFER2_buffer_op));
  assign and_1_out = OP & multiplexer_9_out;  // AND_Gate and_1, 16 bits wide
  assign or_2_out = OP | multiplexer_9_out;  // OR_Gate or_2, 16 bits wide
  assign xor_1_out = OP ^ multiplexer_9_out;  // XOR_Gate xor_1, 16 bits wide
  Buffering BUFFER3 (.BUFFER_IP(BUFFER2_buffer_op), .BUFFER_OP(BUFFER3_buffer_op));
  Multiplexer #(.enable("true"), .select(3), .width(16)) multiplexer_6 (
    .in0(A_q), .in1(B_q), .in2(C_q), .in3(D_q), .in4(E_q), .in5(F_q), .in6(BP_q), .in7(SP_q),
    .out(multiplexer_6_out), .sel(SRC2), .en(SRC2_ENABLE));
  REG_Decoder LOAD_SELECT (
    .IP(DST), .ENABLE(OUT_ENABLE), .A(AS), .B(BS), .C(CS), .D(DS), .s(ES), .t(FS), .BP(BPS), .SP(SPS));
  Multiplexer #(.enable("true"), .select(3), .width(16)) multiplexer_7 (
    .in0(A_q), .in1(B_q), .in2(C_q), .in3(D_q), .in4(E_q), .in5(F_q), .in6(BP_q), .in7(SP_q),
    .out(multiplexer_7_out), .sel(SRC1), .en(SRC1_ENABLE));
  Subtractor #(.width(16)) subtractor_1 (.a(SP_q), .b({16{1'b0}}), .out(subtractor_1_out), .bin(POP));  // open: bout
  Multiplexer #(.width(16)) multiplexer_8 (.in0(multiplexer_7_out), .in1(SRC1_IMM), .out(OP), .sel(IMM1_EN));
  Multiplexer #(.width(16)) multiplexer_9 (
    .in0(multiplexer_6_out), .in1(SRC2_IMM), .out(multiplexer_9_out), .sel(IMM2_EN));
  Buffering BUFFER4 (.BUFFER_IP(BUFFER3_buffer_op), .BUFFER_OP(CLOCK2));
  Multiplexer #(.width(16)) multiplexer_10 (.in0(multiplexer_9_out), .in1(subtractor_1_out), .out(ADDR), .sel(PSHPOP));
  Shifter #(.width(16)) shifter_1 (.in(OP), .\dist (4'b0001), .out(shifter_1_out));
  Shifter #(.shift("lr"), .width(16)) shifter_2 (.in(OP), .\dist (4'b0001), .out(shifter_2_out));
  Adder #(.width(16)) adder_1 (.a(OP), .b(multiplexer_9_out), .out(adder_1_out));  // open: cin, cout
  Subtractor #(.width(16)) subtractor_2 (.a(OP), .b(multiplexer_9_out), .out(subtractor_2_out));  // open: bin, bout
  Comparator #(.mode("unsigned"), .width(16)) comparator_1 (
    .a(OP), .b(multiplexer_9_out), .gt(comparator_1_gt[0]), .eq(comparator_1_gt[1]), .lt(comparator_1_gt[2]));
  and and_2 (PUSH, WRT_t, INV_VAL);
  and and_3 (POP, READ, INV_VAL);
  or or_3 (PSHPOP, PUSH, POP);
  Register #(.width(3)) register_2 (.D(comparator_1_gt), .en(CMP), .clk(CLOCK4), .Q(register_2_q), .clr(Reset));
  or or_4 (or_4_out, JL, JE, JG, JMP);
  assign controlled_buffer_1_out = or_4_out ? INV_VAL : 1'bz;  // Controlled_Buffer controlled_buffer_1
  and and_4 (and_4_out, JG, register_2_q[0]);
  and and_5 (and_5_out, JE, register_2_q[1]);
  and and_6 (and_6_out, JL, register_2_q[2]);
  or or_5 (or_5_out, and_6_out, and_5_out, and_4_out, JMP);
  xor xor_2 (xor_2_out, or_5_out, controlled_buffer_1_out);
  buf buffer_1 (buffer_1_out, CLOCK3);
  buf buffer_2 (buffer_2_out, buffer_1_out);
  buf buffer_3 (Clock_OU, buffer_2_out);
  Counter #(.max('hffff), .trigger("falling"), .width(16)) counter_1 (
    .clr(Reset), .load(xor_2_out), .clk(Clock_IN), .D(OP), .Q(Instruction_Pointer));  // open: up, count, carry
  and and_7 (WRT, WRT_t, CLOCK3);

  // Other names for the same wires on the sheet: CLOCK0 = Clock_IN; IP[15:0] = INSTRUCTION
endmodule

module CPU_Decoder (
  input  [3:0] OPCODE,
  input  UNENABLE,
  output NOOP,
  output MOV,
  output AMD,
  output OW,
  output XOW,
  output ADD,
  output SUB,
  output SHL,
  output SHR,
  output CMP,
  output JMP,
  output JE,
  output JL,
  output JG,
  output WRT,
  output READ,
  output SRC_1,
  output SRC_2,
  output OU
);

  wire not_1_out;

  not not_1 (not_1_out, UNENABLE);
  Decoder #(.select(4)) decoder_1 (
    .out0(NOOP), .out1(MOV), .out2(AMD), .out3(OW), .out4(XOW), .out5(ADD), .out6(SUB), .out7(SHL),
    .out8(SHR), .out9(CMP), .out10(JMP), .out11(JE), .out12(JL), .out13(JG), .out14(WRT), .out15(READ),
    .sel(OPCODE), .en(not_1_out));
  nor nor_1 (OU, NOOP, CMP, JMP, JE, JL, JG, WRT, UNENABLE);
  nor nor_2 (SRC_1, NOOP, READ, UNENABLE);
  or or_1 (SRC_2, AMD, OW, XOW, WRT, ADD, SUB, CMP, READ);
endmodule

module REG_Decoder (
  input  [2:0] IP,
  input  ENABLE,
  output A,
  output B,
  output C,
  output D,
  output s,
  output t,
  output BP,
  output SP
);

  Demultiplexer #(.select(3)) demultiplexer_1 (
    .out0(A), .out1(B), .out2(C), .out3(D), .out4(s), .out5(t), .out6(BP), .out7(SP), .in(ENABLE), .sel(IP));
endmodule

module Buffering (
  input  BUFFER_IP,
  output BUFFER_OP
);

  wire buffer_1_out, buffer_2_out, buffer_3_out, buffer_4_out, buffer_5_out, buffer_6_out, buffer_7_out,
       buffer_8_out, buffer_9_out;

  buf buffer_1 (buffer_1_out, BUFFER_IP);
  buf buffer_2 (buffer_2_out, buffer_1_out);
  buf buffer_3 (buffer_3_out, buffer_2_out);
  buf buffer_4 (buffer_4_out, buffer_3_out);
  buf buffer_5 (buffer_5_out, buffer_4_out);
  buf buffer_6 (buffer_6_out, buffer_5_out);
  buf buffer_7 (buffer_7_out, buffer_6_out);
  buf buffer_8 (buffer_8_out, buffer_7_out);
  buf buffer_9 (buffer_9_out, buffer_8_out);
  buf buffer_10 (BUFFER_OP, buffer_9_out);
endmodule

module IMM_SAVE (
  input  [1:0] IMM_VALS,
  input  [15:0] INSTR_IN,
  input  Clock,
  input  Reset,
  output [15:0] INSTRUCTION,
  output OPCODE_DISABLE,
  output SRC1_IMM,
  output [15:0] SRC1,
  output SRC2_IMM,
  output [15:0] SRC2
);

  wire and_1_out, and_2_out, and_3_out, and_4_out, decoder_1_out1, decoder_1_out2, decoder_1_out3, IMM_EN3_1,
       IMM_EN3_2, IMM_EN_SRC1, IMM_EN_SRC2, IP_ENABLE, not_1_out, not_2_out, not_3_out, not_4_out, not_5_out,
       or_3_out, or_4_out, or_5_out, SINGLE_IMM, WRT_EN, xor_1_out;

  or or_1 (SINGLE_IMM, IMM_VALS[0], IMM_VALS[1]);
  Decoder #(.select(2)) decoder_1 (
    .out1(decoder_1_out1), .out2(decoder_1_out2), .out3(decoder_1_out3), .sel(IMM_VALS), .en(IP_ENABLE));  // open: out0
  or or_2 (WRT_EN, decoder_1_out3, decoder_1_out2, decoder_1_out1);
  and and_1 (and_1_out, not_2_out, decoder_1_out1);
  and and_2 (and_2_out, not_3_out, decoder_1_out2);
  and and_3 (and_3_out, not_1_out, decoder_1_out3);
  not not_1 (not_1_out, IMM_EN3_1);
  D_Flip_Flop #(.trigger("falling")) d_ff_1 (
    .D(and_3_out), .clk(Clock), .Q(IMM_EN3_1), .reset(Reset));  // open: Qn, preset
  not not_2 (not_2_out, IMM_EN_SRC2);
  D_Flip_Flop #(.trigger("falling")) d_ff_2 (
    .D(and_1_out), .clk(Clock), .Q(IMM_EN_SRC2), .reset(Reset));  // open: Qn, preset
  not not_3 (not_3_out, IMM_EN_SRC1);
  D_Flip_Flop #(.trigger("falling")) d_ff_3 (
    .D(and_2_out), .clk(Clock), .Q(IMM_EN_SRC1), .reset(Reset));  // open: Qn, preset
  and and_4 (and_4_out, not_4_out, IMM_EN3_1);
  Register #(.width(16)) register_1 (.D(INSTR_IN), .en(WRT_EN), .clk(Clock), .Q(INSTRUCTION), .clr(Reset));
  not not_4 (not_4_out, IMM_EN3_2);
  D_Flip_Flop #(.trigger("falling")) d_ff_4 (
    .D(and_4_out), .clk(Clock), .Q(IMM_EN3_2), .reset(Reset));  // open: Qn, preset
  or or_3 (or_3_out, IMM_EN_SRC1, IMM_EN3_1);
  or or_4 (or_4_out, IMM_EN_SRC2, IMM_EN3_2);
  Register #(.width(16)) register_2 (.D(INSTR_IN), .en(or_3_out), .clk(Clock), .Q(SRC1), .clr(Reset));
  Register #(.width(16)) register_3 (.D(INSTR_IN), .en(or_4_out), .clk(Clock), .Q(SRC2), .clr(Reset));
  or or_5 (or_5_out, IMM_EN_SRC1, IMM_EN_SRC2, IMM_EN3_2);
  not not_5 (not_5_out, or_5_out);
  xor xor_1 (xor_1_out, SINGLE_IMM, or_5_out);
  xor xor_2 (IP_ENABLE, not_5_out, IMM_EN3_1);
  or or_6 (OPCODE_DISABLE, xor_1_out, IMM_EN3_1);
  or or_7 (SRC1_IMM, IMM_EN3_2, IMM_EN_SRC1);
  or or_8 (SRC2_IMM, IMM_EN3_2, IMM_EN_SRC2);

  // Other names for the same wires on the sheet: INSTR[15:0] = INSTRUCTION
endmodule

module RWControl (
  input  [15:0] Instr,
  input  [15:0] Data,
  input  Write,
  input  Read,
  input  ClkIN,
  input  [15:0] ValIN,
  output [15:0] Addr,
  output WRT,
  output ClkOU,
  output [15:0] ValOU
);

  wire and_1_out, or_1_out;

  and and_1 (and_1_out, or_1_out, ClkIN);
  or or_1 (or_1_out, Write, Read);
  Multiplexer #(.width(16)) multiplexer_1 (.in0(Instr), .in1(Data), .out(Addr), .sel(and_1_out));
  Buffering buffering_1 (.BUFFER_IP(ClkIN), .BUFFER_OP(ClkOU));

  assign ValOU = ValIN;
  assign WRT = Write;
endmodule
